# Fritzing sketch als (saved by Fritzing 0.7.10b)
breadboards: 1

parts:
  R1 = Resistor [tolerance=±5% resistance=220 package=THT]
  LED3 = LED - 5mm [color="Blue (470nm)" package="5 mm [THT]"]
  LED2 = LED - 5mm [color="Red (633nm)" package="5 mm [THT]"]
  R4 = Resistor [tolerance=±5% resistance=220 package=THT]
  R3 = Resistor [tolerance=±5% resistance=220 package=THT]
  LED4 = LED - 5mm [color="Blue (470nm)" package="5 mm [THT]"]
  Arduino1 = Arduino
  J1 = Piezo Speaker
  R5 = Resistor [tolerance=±5% resistance=220 package=THT]
  LED1 = LED - 5mm [color="Red (633nm)" package="5 mm [THT]"]
  R2 = Resistor [tolerance=±5% resistance=220 package=THT]

nets:
  N1: R1.Pin_0, Arduino1.D2
  N2: R1.Pin_1, LED1.cathode
  N3: LED3.cathode, R3.Pin_1
  N4: LED3.anode, LED2.anode, LED4.anode, Arduino1.GND, J1.pin1, LED1.anode
  N5: LED2.cathode, R2.Pin_1
  N6: R4.Pin_0, Arduino1.D8
  N7: R4.Pin_1, LED4.cathode
  N8: R3.Pin_0, Arduino1.D7
  N9: Arduino1.D6, R5.Pin_1
  N10: Arduino1.D4, R2.Pin_0
  N11: J1.pin2, R5.Pin_0
